// Logisim project Assignment_Iguess.circ as structural Verilog: 2 circuits, main circuit main
module main (
  input  in_1
);

  wire Ce, Clk, Cp, Ei, Eo, Ep, Eu, La, Lb, Lc, Li, Lm, Lo, Lr;
  wire [3:0] controlled_buffer_1_out, controlled_buffer_2_out, counter_1_q, ram_1_data, register_1_q;
  wire [7:0] adder_1_out, controlled_buffer_3_out, controlled_buffer_5_out, controlled_buffer_6_out,
       controlled_buffer_8_out, register_2_q, register_3_q, register_4_q, register_5_q;

  Counter #(.width(4), .max('hf)) counter_1 (
    .load(Lc), .D(controlled_buffer_1_out), .count(Cp), .Q(counter_1_q), .clk(Clk), .clr(in_1));  // open: carry
  Register #(.width(4)) register_1 (.D(controlled_buffer_2_out), .Q(register_1_q), .clk(Clk), .clr(in_1));  // open: en
  assign controlled_buffer_1_out = Ep ? counter_1_q : 4'bz;  // Controlled_Buffer controlled_buffer_1
  assign controlled_buffer_2_out = Lm ? controlled_buffer_1_out : 4'bz;  // Controlled_Buffer controlled_buffer_2
  Register register_2 (.D(controlled_buffer_3_out), .Q(register_2_q), .clk(Clk), .clr(in_1));  // open: en
  RAM #(.addrWidth(4), .bus("separate")) ram_1 (
    .addr(register_1_q), .din({ram_1_data, controlled_buffer_1_out}),
    .data({ram_1_data, controlled_buffer_1_out}), .str(Lr), .sel(1'b1), .clk(Clk), .ld(Ce));  // open: clr
  assign controlled_buffer_3_out = Li ? {ram_1_data, controlled_buffer_1_out} : 8'bz;  // Controlled_Buffer controlled_buffer_3
  assign controlled_buffer_1_out = Ei ? register_2_q[3:0] : 4'bz;  // Controlled_Buffer controlled_buffer_4
  Control_Unit control_unit_1 (
    .in_1(in_1), .in_2(Clk), .out_4({Eo, Lo, Eu, Lb, La, Ei, Li, Lr, Ce, Lm, Ep, Cp, Lc}),
    .in_3(register_2_q[7:4]));
  assign controlled_buffer_5_out = La ? {ram_1_data, controlled_buffer_1_out} : 8'bz;  // Controlled_Buffer controlled_buffer_5
  assign controlled_buffer_6_out = Lb ? {ram_1_data, controlled_buffer_1_out} : 8'bz;  // Controlled_Buffer controlled_buffer_6
  assign {ram_1_data, controlled_buffer_1_out} = Eu ? adder_1_out : 8'bz;  // Controlled_Buffer controlled_buffer_7
  assign controlled_buffer_8_out = Lo ? {ram_1_data, controlled_buffer_1_out} : 8'bz;  // Controlled_Buffer controlled_buffer_8
  assign {ram_1_data, controlled_buffer_1_out} = Eo ? register_5_q : 8'bz;  // Controlled_Buffer controlled_buffer_9
  Register register_3 (.D(controlled_buffer_5_out), .Q(register_3_q), .clk(Clk), .clr(in_1));  // open: en
  Register register_4 (.D(controlled_buffer_6_out), .Q(register_4_q), .clk(Clk), .clr(in_1));  // open: en
  Register register_5 (.D(controlled_buffer_8_out), .Q(register_5_q), .clk(Clk), .clr(in_1));  // open: en
  Clock clock_1 (.out(Clk));
  Adder adder_1 (.a(register_3_q), .b(register_4_q), .out(adder_1_out));  // open: cin, cout

  // Other names for the same wires on the sheet: Clr = in_1
endmodule

module Control_Unit (
  input  in_1,
  input  in_2,
  input  [3:0] in_3,
  output [12:0] out_4
);

  wire C, not_1_out, shift_register_1_q0, shift_register_1_q1, shift_register_1_q2, shift_register_1_q3,
       shift_register_1_q4, shift_register_1_q5;
  wire [4:0] A, adder_1_out, adder_2_out, D;

  ROM #(.addrWidth(5), .dataWidth(13)) rom_1 (.addr(A), .data(out_4));  // open: sel
  not not_1 (not_1_out, in_1);
  ROM #(.addrWidth(4), .dataWidth(5)) rom_2 (.addr(in_3), .data(D));  // open: sel
  Shift_Register #(.length(6)) shift_register_1 (
    .shift(not_1_out), .in(C), .clk(in_2), .out(C), .load(in_1), .d0(1'b1), .q0(shift_register_1_q0),
    .d1(1'b0), .q1(shift_register_1_q1), .d2(1'b0), .q2(shift_register_1_q2), .d3(1'b0),
    .q3(shift_register_1_q3), .d4(1'b0), .q4(shift_register_1_q4), .d5(1'b0), .q5(shift_register_1_q5));  // open: clr
  assign A = shift_register_1_q0 ? {5{1'b0}} : 5'bz;  // Controlled_Buffer controlled_buffer_1
  assign A = shift_register_1_q1 ? 5'b00001 : 5'bz;  // Controlled_Buffer controlled_buffer_2
  assign A = shift_register_1_q2 ? 5'b00010 : 5'bz;  // Controlled_Buffer controlled_buffer_3
  assign A = shift_register_1_q4 ? adder_1_out : 5'bz;  // Controlled_Buffer controlled_buffer_4
  assign A = shift_register_1_q3 ? D : 5'bz;  // Controlled_Buffer controlled_buffer_5
  Adder #(.width(5)) adder_1 (.a(D), .b(5'b00001), .out(adder_1_out));  // open: cin, cout
  Adder #(.width(5)) adder_2 (.a(D), .b(5'b00010), .out(adder_2_out));  // open: cin, cout
  assign A = shift_register_1_q5 ? adder_2_out : 5'bz;  // Controlled_Buffer controlled_buffer_6

  // Other names for the same wires on the sheet: B[4:0] = A

  // Notes on the sheet:
  //   contents of rom_1 (hex, n*v repeats v):
  //   c 2 50 88 110 0 88 210 0 c00 0 0 88 1020 0 81
  //   contents of rom_2 (hex, n*v repeats v):
  //   0 3 6 9 c f
endmodule
